# Fritzing sketch pictureframe (saved by Fritzing 0.9.3b)
breadboards: 1

parts:
  Bi-Directional_Logic_Level_Shifter = Adafruit 4-channel I2C-safe Bi-directional Logic Level Converter [part_number="Adafruit #757"]
  V1 = DC Power [voltage=5]
  Raspberry_Pi_1 = Raspberry Pi 3 [part_number=RPI-3-V1.2]
  Part2 = Adafruit TSL2591 [part_number="Adafruit #1980"]

nets:
  GND: Bi-Directional_Logic_Level_Shifter.GND, V1.V-, Raspberry_Pi_1.GND, Part2.GND
  N1: Bi-Directional_Logic_Level_Shifter.A1, Raspberry_Pi_1.GIPO18
  3V3: Bi-Directional_Logic_Level_Shifter.LV, Raspberry_Pi_1.3v3, Raspberry_Pi_1.3V3, Part2.3.3V
  edp PWM brightness control (pin 8): Bi-Directional_Logic_Level_Shifter.B1
  N2: Bi-Directional_Logic_Level_Shifter.HV, V1.V+, Raspberry_Pi_1.5V
  N3: Raspberry_Pi_1.GPIO2, Part2.SDA
  N4: Raspberry_Pi_1.GPIO3, Part2.SCL

notes:
  5V supply provided by USB car charger. Car charger steps down from 12V power supply
  Controller board for the Screen takes 12V and connects to the pi via this PWM pin and through an HDMI cable. The controller board connects to the screen via an edp ribbon cable.

custom parts:
  Adafruit 4-channel I2C-safe Bi-directional Logic Level Converter: Because the Arduino (and Basic Stamp) are 5V devices, and most modern sensors, displays, flash cards and modes are 3.3V-only, many makers find that they need to perform level shifting/conversion to protect the 3.3V device from 5V. We do have some other handy level shifters in the shop, from the DIP 74LVC245 to the fancy bi-directional TXB0108. However, neither of these are happy to work with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
  Adafruit TSL2591: When the future is dazzlingly-bright, this ultra-high-range luminosity sensor will help you measure it. The TSL2591 luminosity sensor is an advanced digital light sensor, ideal for use in a wide range of light situations. Compared to low cost CdS cells, this sensor is more precise, allowing for exact lux calculations and can be configured for different gain/timing ranges to detect light ranges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
